# Fritzing sketch controller (saved by Fritzing 0.9.3b)
circuit board: 7cm x 3cm
breadboards: 1

parts:
  Part1 = Arduino Nano (Rev3.0)
  Part2 = Barometric Pressure Sensor - BMP180 Breakout (GY-68)
  J2 = female pin header, 4 pins [form="♀ (female)"]
  J3 = female pin header, 4 pins [form="♀ (female)"]
  J4 = female pin header, 4 pins [form="♀ (female)"]
  J5 = female pin header, 2 pins [form="♀ (female)"]
  J6 = female pin header, 15 pins [form="♀ (female)"]
  J8 = female pin header, 7 pins [form="♀ (female)"]
  Part3 = InvenSense MPU6050
  J18 = female pin header, 8 pins [form="♀ (female)"]
  J19 = female pin header, 2 pins [form="♀ (female)"]
  J20 = female pin header, 1 pin [form="♀ (female)"]
  J22 = female pin header, 4 pins [form="♀ (female)"]
  J27 = female pin header, 1 pin [form="♀ (female)"]
  J28 = female pin header, 1 pin [form="♀ (female)"]
  J7 = female pin header, 12 pins [form="♀ (female)"]
  J29 = female pin header, 1 pin [form="♀ (female)"]
  J30 = female pin header, 1 pin [form="♀ (female)"]
  J31 = female pin header, 1 pin [form="♀ (female)"]
  J32 = female pin header, 1 pin [form="♀ (female)"]
  J26 = female pin header, 2 pins [form="♀ (female)"]
  J33 = female pin header, 2 pins [form="♀ (female)"]
  J34 = female pin header, 2 pins [form="♀ (female)"]
  J35 = female pin header, 1 pin [form="♀ (female)"]
  J36 = female pin header, 1 pin [form="♀ (female)"]
  J37 = female pin header, 1 pin [form="♀ (female)"]  # not connected

nets (from the pcb view):
  N1: Part1.D1/TX, J6.pin1, J19.pin2
  N2: Part1.D0/RX, J6.pin2, J19.pin1
  N3: Part1.RESET, J6.pin3, J18.pin3
  N4: Part1.GND, J5.pin2, J6.pin4, J18.pin2, J7.pin1, J7.pin2, J7.pin3, J7.pin4, J7.pin5, J7.pin6, J7.pin7, J7.pin8, J7.pin9, J7.pin10, J7.pin11, J7.pin12, J26.pin2, J33.pin1, J35.pin1, J36.pin1
  N5: Part1.D2, J6.pin5
  N6: Part1.D3, J6.pin6
  N7: Part1.D4, J6.pin7
  N8: Part1.D5, J6.pin8
  N9: Part1.D6, J6.pin9
  N10: Part1.D7, J6.pin10
  N11: Part1.D8, J6.pin11
  N12: Part1.D9, J6.pin12
  N13: Part1.D10, J6.pin13
  N14: Part1.D11/MOSI, J6.pin14
  N15: Part1.D12/MISO, J6.pin15
  N16: Part1.VIN, J5.pin1, J18.pin1, J26.pin1, J33.pin2
  VCC: Part1.5V, Part2.VCC, J2.pin1, J3.pin4, J4.pin1, Part3.VCC, J18.pin4, J22.pin1
  N17: Part1.A7, J18.pin5
  N18: Part1.A6, J18.pin6
  N19: Part1.A5, Part2.SCL, J2.pin3, J3.pin2, J4.pin3, Part3.SCL, J18.pin7, J22.pin3, J29.pin1, J30.pin1
  N20: Part1.A4, Part2.SDA, J2.pin4, J3.pin1, J4.pin4, Part3.SDA, J18.pin8, J22.pin4, J31.pin1, J32.pin1
  N21: Part1.A3, J8.pin1
  N22: Part1.A2, J8.pin2
  N23: Part1.A1, J8.pin3
  N24: Part1.A0, J8.pin4, J20.pin1
  N25: Part1.AREF, J8.pin5
  N26: Part1.3V3, J8.pin6
  N27: Part1.D13/SCK, J8.pin7
  GND: Part2.GND, J2.pin2, J3.pin3, J4.pin2, Part3.GND, J27.pin1, J28.pin1
  N28: J34.pin1, J34.pin2

notes:
  +
  -
  IMU
  COMP
  A0
  R1
  R2
