# Fritzing sketch flightcontroller_rpi (saved by Fritzing 0.9.3b)
circuit board: 7cm x 6cm

parts:
  Part1 = Arduino Nano (Rev3.0)
  Part2 = InvenSense MPU6050
  J1 = female pin header, 11 pins [form="♀ (female)"]
  J3 = female pin header, 4 pins [form="♀ (female)"]
  J2 = female pin header, 11 pins [form="♀ (female)"]
  J4 = female pin header, 2 pins [form="♀ (female)"]
  J6 = female pin header, 2 pins [form="♀ (female)"]
  J7 = female pin header, 2 pins [form="♀ (female)"]
  J8 = female pin header, 1 pin [form="♀ (female)"]
  J9 = female pin header, 1 pin [form="♀ (female)"]
  J12 = female pin header, 4 pins [form="♀ (female)"]
  J13 = female pin header, 4 pins [form="♀ (female)"]
  J14 = female pin header, 4 pins [form="♀ (female)"]
  J17 = female pin header, 4 pins [form="♀ (female)"]
  J11 = female pin header, 2 pins [form="♀ (female)"]

nets (from the pcb view):
  N1: Part1.D1/TX, J11.pin1
  N2: Part1.D0/RX, J11.pin2
  GND: Part1.GND, Part2.GND, J3.pin3, J2.pin1, J2.pin11, J4.pin2, J6.pin2, J7.pin1, J12.pin2, J13.pin2, J17.pin2
  N3: Part1.D2, J1.pin1
  N4: Part1.D3, J1.pin2
  N5: Part1.D4, J1.pin3
  N6: Part1.D5, J1.pin4
  N7: Part1.D6, J1.pin5
  N8: Part1.D7, J1.pin6
  N9: Part1.D8, J1.pin7
  N10: Part1.D9, J1.pin8
  N11: Part1.D10, J1.pin9
  N12: Part1.D11/MOSI, J1.pin10
  N13: Part1.D12/MISO, J1.pin11
  N14: Part1.VIN, J4.pin1, J6.pin1, J7.pin2
  5V: Part1.5V, Part2.VCC, J3.pin4, J12.pin1, J13.pin1, J14.pin1, J17.pin1
  N15: Part1.A5, Part2.SCL, J3.pin2, J8.pin1, J9.pin1, J12.pin3, J13.pin3
  N16: Part1.A4, J3.pin1, J12.pin4, J13.pin4

notes:
  +
  -
