# Fritzing sketch fcV2Nrf (saved by Fritzing 0.9.3b)
circuit board: 6cm x 3cm

parts:
  Nano = Arduino Nano (Rev3.0)
  Eng = female pin header, 2 pins [form="♀ (female)"]
  Eng1 = female pin header, 2 pins [form="♀ (female)"]  # not connected
  Eng2 = female pin header, 1 pin [form="♀ (female)"]
  Eng3 = female pin header, 1 pin [form="♀ (female)"]
  Eng4 = female pin header, 1 pin [form="♀ (female)"]
  Eng5 = female pin header, 1 pin [form="♀ (female)"]
  3V_Source5 = Battery
  3V_Source6 = Battery
  3V_Source7 = Battery
  3V_Source8 = Battery
  Eng6 = female pin header, 6 pins [form="♀ (female)"]
  Eng7 = female pin header, 1 pin [form="♀ (female)"]
  Eng8 = female pin header, 1 pin [form="♀ (female)"]
  Eng9 = female pin header, 1 pin [form="♀ (female)"]
  Eng10 = female pin header, 1 pin [form="♀ (female)"]
  Eng11 = female pin header, 1 pin [form="♀ (female)"]
  Eng12 = female pin header, 1 pin [form="♀ (female)"]
  Eng13 = female pin header, 4 pins [form="♀ (female)"]
  Eng14 = female pin header, 4 pins [form="♀ (female)"]
  Eng15 = female pin header, 4 pins [form="♀ (female)"]  # not connected
  Eng16 = female pin header, 4 pins [form="♀ (female)"]  # not connected
  Eng17 = female pin header, 4 pins [form="♀ (female)"]  # not connected
  Eng18 = female pin header, 4 pins [form="♀ (female)"]  # not connected
  Eng19 = female pin header, 4 pins [form="♀ (female)"]
  Eng20 = female pin header, 14 pins [form="♀ (female)"]
  Eng21 = female pin header, 1 pin [form="♀ (female)"]
  Eng22 = female pin header, 1 pin [form="♀ (female)"]
  Eng23 = female pin header, 1 pin [form="♀ (female)"]
  Eng24 = female pin header, 1 pin [form="♀ (female)"]
  Eng25 = female pin header, 2 pins [form="♀ (female)"]
  Eng26 = female pin header, 2 pins [form="♀ (female)"]
  Eng27 = female pin header, 1 pin [form="♀ (female)"]
  Eng28 = female pin header, 1 pin [form="♀ (female)"]
  3V_Source9 = Battery
  Eng29 = female pin header, 1 pin [form="♀ (female)"]
  Eng30 = female pin header, 1 pin [form="♀ (female)"]  # not connected
  Eng31 = female pin header, 1 pin [form="♀ (female)"]
  Eng32 = female pin header, 1 pin [form="♀ (female)"]
  Eng33 = female pin header, 1 pin [form="♀ (female)"]
  Eng34 = female pin header, 1 pin [form="♀ (female)"]
  Eng35 = female pin header, 1 pin [form="♀ (female)"]
  Eng36 = female pin header, 1 pin [form="♀ (female)"]

nets:
  N1: Nano.D1/TX, Eng25.pin2, Eng26.pin2
  N2: Nano.D0/RX, Eng25.pin1, Eng26.pin1
  N3: Nano.GND, Eng2.pin1, Eng5.pin1, 3V_Source7.-, 3V_Source8.-, Eng6.pin5, Eng12.pin1, Eng20.pin13, Eng27.pin1, 3V_Source9.-
  N4: Nano.D2, Eng21.pin1
  N5: Nano.D3, Eng3.pin1
  N6: Nano.D4, Eng22.pin1
  N7: Nano.D5, Eng.pin2
  N8: Nano.D6, Eng.pin1
  N9: Nano.D7, Eng23.pin1
  N10: Nano.D8, Eng24.pin1
  N11: Nano.D9, Eng4.pin1
  N12: Nano.D10, Eng28.pin1
  N13: Nano.D11/MOSI, Eng34.pin1
  N14: Nano.D12/MISO, Eng35.pin1
  N15: Nano.VIN, 3V_Source7.+, 3V_Source8.+, Eng11.pin1, Eng20.pin14, 3V_Source9.+
  N16: Nano.RESET, Eng20.pin12
  N17: Nano.5V, Eng6.pin6, Eng7.pin1, Eng8.pin1, Eng20.pin11
  N18: Nano.A7, Eng20.pin10
  N19: Nano.A6, Eng20.pin9
  N20: Nano.A5, Eng6.pin4, Eng14.pin2, Eng19.pin2, Eng20.pin8
  N21: Nano.A4, Eng6.pin3, Eng9.pin1, Eng10.pin1, Eng20.pin7
  N22: Nano.A3, Eng20.pin6
  N23: Nano.A2, Eng20.pin5
  N24: Nano.A1, Eng20.pin4
  N25: Nano.A0, Eng20.pin3, Eng29.pin1, Eng31.pin1
  N26: Nano.AREF, Eng20.pin2
  N27: Nano.3V3, Eng20.pin1
  N28: Nano.D13/SCK, Eng36.pin1
  N29: 3V_Source5.-, 3V_Source6.-
  N30: 3V_Source5.+, 3V_Source6.+
  N31: Eng13.pin1, Eng14.pin4, Eng19.pin4
  N32: Eng13.pin2, Eng14.pin3, Eng19.pin3
  N33: Eng13.pin4, Eng14.pin1, Eng19.pin1
  N34: Eng32.pin1, Eng33.pin1

notes:
  -
  +
  1
  2
  cmb87
