# Fritzing sketch fcV2Nrf_esc (saved by Fritzing 0.9.3b)
circuit board: 1.2cm x 1cm

parts:
  D1 = Schottky Diode [part_number=1N5817 package="300 mil [THT]"]
  R1 = Resistor [tolerance=±5% resistance=220 package=THT]
  Eng8 = female pin header, 2 pins [form="♀ (female)"]
  Eng7 = female pin header, 1 pin [form="♀ (female)"]
  Eng10 = female pin header, 1 pin [form="♀ (female)"]
  Eng11 = female pin header, 1 pin [form="♀ (female)"]
  Q3 = PNP-Transistor [package="SOT-23 [SMD]"]

nets:
  N1: D1.cathode, Eng8.pin1, Q3.1
  N2: D1.anode, Eng8.pin2, Eng7.pin1
  N3: R1.Pin_0, Eng11.pin1, Q3.2
  N4: R1.Pin_1, Eng10.pin1, Q3.0

notes:
  +
  -
