# Fritzing sketch fcV2Nrf_escboard (saved by Fritzing 0.9.3b)
circuit board: 3.2cm x 1.9cm

parts:
  Q5 = PNP-Transistor [package="SOT-23 [SMD]"]
  Eng12 = female pin header, 2 pins [form="♀ (female)"]
  Eng13 = female pin header, 2 pins [form="♀ (female)"]
  D2 = Schottky Diode [part_number=1N5817 package="300 mil [THT]"]
  R2 = Resistor [tolerance=±5% resistance=220 package=THT]
  Eng14 = female pin header, 1 pin [form="♀ (female)"]
  Eng15 = female pin header, 2 pins [form="♀ (female)"]
  D3 = Schottky Diode [part_number=1N5817 package="300 mil [THT]"]
  R3 = Resistor [tolerance=±5% resistance=220 package=THT]
  Q6 = PNP-Transistor [package="SOT-23 [SMD]"]
  J1 = female pin header, 6 pins [form="♀ (female)"]
  Eng16 = female pin header, 1 pin [form="♀ (female)"]
  Eng17 = female pin header, 2 pins [form="♀ (female)"]
  D4 = Schottky Diode [part_number=1N5817 package="300 mil [THT]"]
  R4 = Resistor [tolerance=±5% resistance=220 package=THT]
  Q7 = PNP-Transistor [package="SOT-23 [SMD]"]
  Eng18 = female pin header, 1 pin [form="♀ (female)"]
  Eng19 = female pin header, 2 pins [form="♀ (female)"]
  D5 = Schottky Diode [part_number=1N5817 package="300 mil [THT]"]
  R5 = Resistor [tolerance=±5% resistance=220 package=THT]
  Q8 = PNP-Transistor [package="SOT-23 [SMD]"]
  Eng20 = female pin header, 1 pin [form="♀ (female)"]
  Eng21 = female pin header, 2 pins [form="♀ (female)"]
  Eng22 = female pin header, 1 pin [form="♀ (female)"]

nets:
  N1: Q5.2, Eng12.pin2, R2.Pin_1, R3.Pin_1, Q6.2, R5.Pin_1, Q8.2
  N2: Q5.0, R2.Pin_0, Eng14.pin1
  N3: Q5.1, Eng13.pin1, D2.cathode
  N4: Eng12.pin1, Eng13.pin2, D2.anode, Eng15.pin2, D3.anode, J1.pin1, Eng17.pin2, D4.anode
  N5: Eng15.pin1, D3.cathode, Q6.1
  N6: R3.Pin_0, Q6.0, Eng16.pin1
  N7: J1.pin2, Eng21.pin2
  N8: Eng17.pin1, D4.cathode, Q7.1
  N9: R4.Pin_0, Q7.0, Eng18.pin1
  N10: R4.Pin_1, Q7.2, Eng22.pin1
  N11: Eng19.pin1, D5.cathode, Q8.1
  N12: Eng19.pin2, D5.anode, Eng21.pin1
  N13: R5.Pin_0, Q8.0, Eng20.pin1

notes:
  +
  S
  -
