# Fritzing sketch fcV2Nrf_upper (saved by Fritzing 0.9.3b)
circuit board: 3.93436cm x 2.31593cm

parts:
  Part1 = NRF24L01+ Breakout Board
  Eng7 = female pin header, 1 pin [form="♀ (female)"]
  Eng9 = female pin header, 1 pin [form="♀ (female)"]
  Eng10 = female pin header, 1 pin [form="♀ (female)"]
  Eng11 = female pin header, 1 pin [form="♀ (female)"]
  Eng12 = female pin header, 1 pin [form="♀ (female)"]
  Eng13 = female pin header, 2 pins [form="♀ (female)"]
  Eng14 = female pin header, 2 pins [form="♀ (female)"]
  Eng15 = female pin header, 1 pin [form="♀ (female)"]
  J1 = female pin header, 2 pins [form="♀ (female)"]
  J2 = female pin header, 2 pins [form="♀ (female)"]
  Eng16 = female pin header, 1 pin [form="♀ (female)"]
  Nano = Arduino Nano (Rev3.0)  # not connected

nets:
  N1: Part1.VCC, Eng13.pin2, Eng14.pin2
  N2: Part1.CE, Eng10.pin1, J2.pin2
  N3: Part1.CS, Eng12.pin1, J2.pin1
  N4: Part1.SCK, Eng7.pin1, Eng16.pin1
  N5: Part1.MOSI, Eng11.pin1, J1.pin2
  N6: Part1.MISO, Eng9.pin1, J1.pin1
  N7: Eng13.pin1, Eng14.pin1, Eng15.pin1

notes:
  -
  +
  w
